# Fritzing sketch empfaenger_sketch (saved by Fritzing 0.9.9b)
breadboards: 1

parts:
  LED8 = LED - 5mm [color="Blue (430nm)" current=0.030 package="5 mm [THT]"]
  LED9 = LED - 5mm [color="Blue (430nm)" current=0.030 package="5 mm [THT]"]
  LED10 = LED - 5mm [color="Blue (430nm)" current=0.030 package="5 mm [THT]"]
  LED11 = LED - 5mm [color="Blue (430nm)" current=0.030 package="5 mm [THT]"]
  LED12 = LED - 5mm [color="Blue (430nm)" current=0.030 package="5 mm [THT]"]
  LED13 = LED - 5mm [color="Blue (430nm)" current=0.030 package="5 mm [THT]"]
  LED14 = LED - 5mm [color="Blue (430nm)" current=0.030 package="5 mm [THT]"]
  LED15 = LED - 5mm [color="Blue (430nm)" current=0.030 package="5 mm [THT]"]
  Bauteil1 = Arduino Mega 2560 (Rev3)
  Bauteil2 = LCD1602-I2C

nets:
  N1: LED8.cathode, Bauteil1.D53
  N2: LED8.anode, LED9.anode, LED10.anode, LED11.anode, LED12.anode, LED13.anode, LED14.anode, LED15.anode
  N3: LED9.cathode, Bauteil1.D51
  N4: LED10.cathode, Bauteil1.D49
  N5: LED11.cathode, Bauteil1.D47
  N6: LED12.cathode, Bauteil1.D45
  N7: LED13.cathode, Bauteil1.D43
  N8: LED14.cathode, Bauteil1.D41
  N9: LED15.cathode, Bauteil1.D39
  N10: Bauteil1.D21/SCL, Bauteil2.SCL
  N11: Bauteil1.D20/SDA, Bauteil2.SDA
  5V: Bauteil1.5V, Bauteil2.VCC
  GND: Bauteil1.GND, Bauteil2.GND

custom parts:
  LCD1602-I2C: A standard character display, usually with 2x16 characters. Comes in many colors with LCM1602 IIC attached.
