# Fritzing sketch sender_sketch (saved by Fritzing 0.9.9b)
breadboards: 1

parts:
  LED8 = LED - 5mm [color="Blue (430nm)" current=0.030 package="5 mm [THT]"]
  LED9 = LED - 5mm [color="Blue (430nm)" current=0.030 package="5 mm [THT]"]
  LED10 = LED - 5mm [color="Blue (430nm)" current=0.030 package="5 mm [THT]"]
  LED11 = LED - 5mm [color="Blue (430nm)" current=0.030 package="5 mm [THT]"]
  LED12 = LED - 5mm [color="Blue (430nm)" current=0.030 package="5 mm [THT]"]
  LED13 = LED - 5mm [color="Blue (430nm)" current=0.030 package="5 mm [THT]"]
  LED14 = LED - 5mm [color="Blue (430nm)" current=0.030 package="5 mm [THT]"]
  LED15 = LED - 5mm [color="Blue (430nm)" current=0.030 package="5 mm [THT]"]
  WeMos_D1_Mini1 = WeMos D1 Mini
  R1 = Resistor [tolerance=±5% power=0.25 resistance=330 package=THT]

nets:
  N1: LED8.cathode, WeMos_D1_Mini1.D5
  N2: LED8.anode, LED9.anode, LED10.anode, LED11.anode, LED12.anode, LED13.anode, LED14.anode, LED15.anode, R1.Pin_0
  N3: LED9.cathode, WeMos_D1_Mini1.D6
  N4: LED10.cathode, WeMos_D1_Mini1.D1
  N5: LED11.cathode, WeMos_D1_Mini1.D2
  N6: LED12.cathode, WeMos_D1_Mini1.D3
  N7: LED13.cathode, WeMos_D1_Mini1.D4
  N8: LED14.cathode, WeMos_D1_Mini1.D7
  N9: LED15.cathode, WeMos_D1_Mini1.D8
  N10: WeMos_D1_Mini1.G, R1.Pin_1
